// Logisim project ALU.circ as structural Verilog: 1 circuit, main circuit ALU
module ALU (
  input  [31:0] A,
  input  [31:0] B,
  input  [4:0] Shift,
  input  CarryIn,
  input  [3:0] Codop,
  output [3:0] Flags,
  output [31:0] S
);

  wire [31:0] AandB, AmBpCm1, ApBpC, AxorB, Blshift, Brashift, Brrshift, Brshift, undriven, undriven_2,
       undriven_3, undriven_4, undriven_5, undriven_6, undriven_7, undriven_8, undriven_9;

  assign AandB = A & B;  // AND_Gate and_1, 32 bits wide
  assign AxorB = A ^ B;  // XOR_Gate xor_1, 32 bits wide
  Shifter #(.width(32)) shifter_1 (.in(B), .\dist (Shift), .out(Blshift));
  Shifter #(.shift("lr"), .width(32)) shifter_2 (.in(B), .\dist (Shift), .out(Brshift));
  Shifter #(.shift("ar"), .width(32)) shifter_3 (.in(B), .\dist (Shift), .out(Brashift));
  Adder #(.width(32)) adder_1 (.a(A), .b(B), .out(ApBpC), .cin(CarryIn));  // open: cout
  Subtractor #(.width(32)) subtractor_1 (.a(A), .b(B), .out(AmBpCm1), .bin(CarryIn));  // open: bout
  Shifter #(.shift("rr"), .width(32)) shifter_4 (.in(B), .\dist (Shift), .out(Brrshift));
  Multiplexer #(.select(4), .width(32)) multiplexer_1 (
    .in0(AandB), .in1(AxorB), .in2(Blshift), .in3(Brshift), .in4(Brashift), .in5(ApBpC), .in6(AmBpCm1),
    .in7(undriven), .in8(undriven_2), .in9(undriven_3), .in10(undriven_4), .in11(undriven_5),
    .in12(undriven_6), .in13(undriven_7), .in14(undriven_8), .in15(undriven_9), .out(S), .sel(Codop));

  // Other names for the same wires on the sheet: CI = CarryIn; Flag[3:0] = Flags

  // Notes on the sheet:
  //   Note: for ROR, C = N
  //   Note 2: assume that shift > 0 for LSL and LSR
endmodule
